# Fritzing sketch prci (saved by Fritzing 0.8.7b)

parts:
  M7 = fc-51 [package=THT]
  M8 = fc-51 [package=THT]
  VCC1 = Battery
  M10 = DC Motor
  M11 = DC Motor
  M12 = DC Motor
  Součástka1 = Arduino Uno (Rev3)  # not connected
  Součástka2 = Rotoshield - Motor driver shield for Arduino
  M9 = DC Motor
  S1 = Square Pushbutton

nets:
  N1: M7.pin1, Součástka2.A_IN_0
  N2: M7.pin2, M8.pin2, VCC1.-, Součástka2.GND
  N3: M7.pin3, M8.pin3, Součástka2.+5V
  N4: M8.pin1, Součástka2.A_IN_1
  N5: VCC1.+, S1.leg0
  N6: M10.pin_1, Součástka2.M4-1
  N7: M10.pin_2, Součástka2.M4-2
  N8: M11.pin_1, Součástka2.M1-1
  N9: M11.pin_2, Součástka2.M1-2
  N10: M12.pin_1, Součástka2.M2-1
  N11: M12.pin_2, Součástka2.M2-2
  N12: Součástka2.M3-2, M9.pin_2
  N13: Součástka2.M3-1, M9.pin_1
  N14: Součástka2.VCC, S1.leg1
