# Fritzing sketch schema (saved by Fritzing 0.8.7b)

parts:
  Součástka2 = Rotoshield - Motor driver shield for Arduino
  Součástka1 = Arduino Uno (Rev3)  # not connected
  VCC2 = Battery
  M7 = DC Motor
  M8 = DC Motor
  M9 = DC Motor
  M10 = DC Motor
  M11 = fc-51 [package=THT]
  M12 = fc-51 [package=THT]

nets:
  N1: Součástka2.A_IN_0, M12.pin1
  N2: Součástka2.A_IN_1, M11.pin1
  N3: Součástka2.+5V, M11.pin3, M12.pin3
  N4: Součástka2.GND, VCC2.-, M11.pin2, M12.pin2
  N5: Součástka2.M1-2, M9.pin_2
  N6: Součástka2.M1-1, M9.pin_1
  N7: Součástka2.M2-2, M10.pin_2
  N8: Součástka2.M2-1, M10.pin_1
  N9: Součástka2.M3-2, M7.pin_2
  N10: Součástka2.M3-1, M7.pin_1
  N11: Součástka2.M4-2, M8.pin_2
  N12: Součástka2.M4-1, M8.pin_1
  N13: Součástka2.VCC, VCC2.+
